# Fritzing sketch Placa Guante (saved by Fritzing 0.9.3b)
circuit board: 6.0716cm x 8.82838cm
breadboards: 1

parts:
  Arduino_Nano_V3 = Arduino Nano (Rev3.0)
  MPU6050 = GY-521 (MPU-6050) [form="♀ (female)" package=THT]
  Bluetooth_HC-05 = Bluetooth HC-05 Macho
  J1 = female pin header, 2 pins [form="♀ (female)"]
  J2 = female pin header, 2 pins [form="♀ (female)"]
  J3 = female pin header, 2 pins [form="♀ (female)"]
  J4 = female pin header, 2 pins [form="♀ (female)"]
  J5 = female pin header, 2 pins [form="♀ (female)"]
  R4 = Resistor [tolerance=±5% resistance=220 package=THT]
  R3 = Resistor [tolerance=±5% resistance=220 package=THT]
  R2 = Resistor [tolerance=±5% resistance=220 package=THT]
  R1 = Resistor [tolerance=±5% resistance=220 package=THT]

nets:
  GND: Arduino_Nano_V3.GND, MPU6050.pin2, Bluetooth_HC-05.GND, R4.Pin_1, R3.Pin_1, R2.Pin_1, R1.Pin_1
  N1: Arduino_Nano_V3.D2, MPU6050.pin5
  N2: Arduino_Nano_V3.D5, Bluetooth_HC-05.TXD
  N3: Arduino_Nano_V3.D6, Bluetooth_HC-05.RXD
  N4: Arduino_Nano_V3.D8, J4.pin2, R4.Pin_0
  N5: Arduino_Nano_V3.D9, J4.pin1, R3.Pin_0
  N6: Arduino_Nano_V3.D10, J2.pin2, R2.Pin_0
  N7: Arduino_Nano_V3.D11/MOSI, J2.pin1, R1.Pin_0
  5V: Arduino_Nano_V3.5V, MPU6050.pin1, Bluetooth_HC-05.VCC, J1.pin2
  N8: Arduino_Nano_V3.A6, J1.pin1
  N9: Arduino_Nano_V3.A5, MPU6050.pin3
  N10: Arduino_Nano_V3.A4, MPU6050.pin4
  N11: Arduino_Nano_V3.A3, J5.pin1
  N12: Arduino_Nano_V3.A2, J5.pin2
  N13: Arduino_Nano_V3.A1, J3.pin1
  N14: Arduino_Nano_V3.A0, J3.pin2

custom parts:
  GY-521 (MPU-6050): Placa GY-521 basada en conjunto de acelerómetro+giroscopios MPU-6050
